// Digital circuit Address_Decode.dig as structural Verilog
module Address_Decode (
  input  A1,
  input  A2,
  input  A3,
  input  A4,
  input  A5,
  input  A6,
  input  A7,
  input  A8,
  input  A9,
  input  A10,
  input  A11,
  input  A12,
  input  A0,
  output _0000_0001,
  output nP1EN,
  output _0004_0005,
  output nACIAEN,
  output _0008_0009,
  output nP2EN,
  output nP3EN,
  output nP4EN,
  output _0000_007F,
  output _0080_00FF,
  output _0100_017F,
  output _0180_01FF,
  output _0200_027F,
  output _0280_02FF,
  output _0300_037F,
  output _0380_03FF,
  output nROMCS,
  output nRAM2CS,
  output nRAMBANK1CS,
  output RTCCS1_2,
  output RTCCS2,
  output nRAM1CS,
  output A0K,
  output RTCCS1,
  output _0000_000F
);

  wire not_1_out, not_4_out, or_1_out, or_4_out;

  _74138 _74138_1 (
    .pin1(A1), .pin2(A2), .pin3(A3), .pin4(1'b0), .pin5(_0000_000F), .pin6(1'b1), .pin7(nP4EN), .pin8(1'b0),
    .pin9(nP3EN), .pin10(nP2EN), .pin11(_0008_0009), .pin12(nACIAEN), .pin13(_0004_0005), .pin14(nP1EN),
    .pin15(_0000_0001), .pin16(1'b1));
  or or_1 (or_1_out, A4, A5, A6);
  _74138 _74138_2 (
    .pin1(A7), .pin2(A8), .pin3(A9), .pin4(1'b0), .pin5(A0K), .pin6(1'b1), .pin7(_0380_03FF), .pin8(1'b0),
    .pin9(_0300_037F), .pin10(_0280_02FF), .pin11(_0200_027F), .pin12(_0180_01FF), .pin13(_0100_017F),
    .pin14(_0080_00FF), .pin15(_0000_007F), .pin16(1'b1));
  or or_2 (A0K, A10, A11, A12);
  or or_3 (_0000_000F, or_1_out, _0000_007F);
  or or_4 (or_4_out, or_1_out, _0100_017F);
  not not_1 (not_1_out, A11);
  not not_2 (nROMCS, A12);
  nand nand_1 (nRAMBANK1CS, not_1_out, nROMCS);
  nand nand_2 (nRAM2CS, A11, nROMCS);
  not not_3 (RTCCS1, or_4_out);
  not not_4 (not_4_out, nRAMBANK1CS);
  nand nand_3 (nRAM1CS, or_4_out, _0000_007F, not_4_out);

  assign RTCCS1_2 = RTCCS1;
  assign RTCCS2 = 1'b1;
endmodule

/* Test case ROM ~CS:
A12 A11 A10 ~ROMCS
1   x   x   0
0   x   x   1
*/

/* Test case RAM2 ~CS:
A12 A11 A10 ~RAM2CS
1   x   x   1
0   0   x   1
0   1   x   0
*/

/* Test case RAM1 ~CS:
A12 A11 A10 A9 A8 A7 A6 A5 A4 ~RAM1CS
# 1000 - 1FFF is ROM
1   x   x   x  x  x  x  x  x  1
# 0800 - 0FFF is RAM2
0   1   x   x  x  x  x  x  x  1
# 0000 - 07FF is RAM1, with exceptions
0   0   1   x  x  x  x  x  x  0
0   0   0   1  x  x  x  x  x  0
0   0   0   0  1  1  x  x  x  0
0   0   0   0  1  0  1  x  x  0
0   0   0   0  1  0  0  1  x  0
0   0   0   0  1  0  0  0  1  0
# 0100 - 010F is RTC
0   0   0   0  1  0  0  0  0  1
# 80 - FF is external RAM
0   0   0   0  0  1  x  x  x  0
# 00 - 7F is internal RAM
0   0   0   0  0  0  x  x  x  1
*/

/* Test case RTC CS1:
A12 A11 A10 A9 A8 A7 A6 A5 A4 RTCCS1
1   x   x   x  x  x  x  x  x  0
0   1   x   x  x  x  x  x  x  0
0   0   1   x  x  x  x  x  x  0
0   0   0   1  x  x  x  x  1  0
0   0   0   0  1  1  x  x  x  0
0   0   0   0  1  0  1  x  x  0
0   0   0   0  1  0  0  1  x  0
0   0   0   0  1  0  0  0  0  1
0   0   0   0  0  1  x  x  x  0
0   0   0   0  0  0  1  x  x  0
0   0   0   0  0  0  0  1  x  0
*/

/* Test case Pair 1 ~EN:
A12 A11 A10 A9 A8 A7 A6 A5 A4 A3 A2 A1 ~P1EN
0   0   0   0  0  0  0  0  0  0  0  0  1
0   0   0   0  0  0  0  0  0  0  0  1  0
0   0   0   0  0  0  0  0  0  0  1  0  1
0   0   0   0  0  0  0  0  0  0  1  1  1
0   0   0   0  0  0  0  0  0  1  0  0  1
0   0   0   0  0  0  0  0  0  1  0  1  1
0   0   0   0  0  0  0  0  0  1  1  0  1
0   0   0   0  0  0  0  0  0  1  1  1  1
x   x   x   x  x  x  x  x  1  x  x  x  1
x   x   x   x  x  x  x  1  0  x  x  x  1
x   x   x   x  x  x  1  0  0  x  x  x  1
x   x   x   x  x  1  0  0  0  x  x  x  1
x   x   x   x  1  0  0  0  0  x  x  x  1
x   x   x   1  0  0  0  0  0  x  x  x  1
x   x   1   0  0  0  0  0  0  x  x  x  1
x   1   0   0  0  0  0  0  0  x  x  x  1
1   0   0   0  0  0  0  0  0  x  x  x  1
*/

/* Test case ACIA ~EN:
A12 A11 A10 A9 A8 A7 A6 A5 A4 A3 A2 A1 ~ACIAEN
0   0   0   0  0  0  0  0  0  0  0  0  1
0   0   0   0  0  0  0  0  0  0  0  1  1
0   0   0   0  0  0  0  0  0  0  1  0  1
0   0   0   0  0  0  0  0  0  0  1  1  0
0   0   0   0  0  0  0  0  0  1  0  0  1
0   0   0   0  0  0  0  0  0  1  0  1  1
0   0   0   0  0  0  0  0  0  1  1  0  1
0   0   0   0  0  0  0  0  0  1  1  1  1
x   x   x   x  x  x  x  x  1  x  x  x  1
x   x   x   x  x  x  x  1  0  x  x  x  1
x   x   x   x  x  x  1  0  0  x  x  x  1
x   x   x   x  x  1  0  0  0  x  x  x  1
x   x   x   x  1  0  0  0  0  x  x  x  1
x   x   x   1  0  0  0  0  0  x  x  x  1
x   x   1   0  0  0  0  0  0  x  x  x  1
x   1   0   0  0  0  0  0  0  x  x  x  1
1   0   0   0  0  0  0  0  0  x  x  x  1
*/

/* Test case Pair 2 ~EN:
A12 A11 A10 A9 A8 A7 A6 A5 A4 A3 A2 A1 ~P2EN
0   0   0   0  0  0  0  0  0  0  0  0  1
0   0   0   0  0  0  0  0  0  0  0  1  1
0   0   0   0  0  0  0  0  0  0  1  0  1
0   0   0   0  0  0  0  0  0  0  1  1  1
0   0   0   0  0  0  0  0  0  1  0  0  1
0   0   0   0  0  0  0  0  0  1  0  1  0
0   0   0   0  0  0  0  0  0  1  1  0  1
0   0   0   0  0  0  0  0  0  1  1  1  1
x   x   x   x  x  x  x  x  1  x  x  x  1
x   x   x   x  x  x  x  1  0  x  x  x  1
x   x   x   x  x  x  1  0  0  x  x  x  1
x   x   x   x  x  1  0  0  0  x  x  x  1
x   x   x   x  1  0  0  0  0  x  x  x  1
x   x   x   1  0  0  0  0  0  x  x  x  1
x   x   1   0  0  0  0  0  0  x  x  x  1
x   1   0   0  0  0  0  0  0  x  x  x  1
1   0   0   0  0  0  0  0  0  x  x  x  1
*/

/* Test case Pair 3 ~EN:
A12 A11 A10 A9 A8 A7 A6 A5 A4 A3 A2 A1 ~P3EN
0   0   0   0  0  0  0  0  0  0  0  0  1
0   0   0   0  0  0  0  0  0  0  0  1  1
0   0   0   0  0  0  0  0  0  0  1  0  1
0   0   0   0  0  0  0  0  0  0  1  1  1
0   0   0   0  0  0  0  0  0  1  0  0  1
0   0   0   0  0  0  0  0  0  1  0  1  1
0   0   0   0  0  0  0  0  0  1  1  0  0
0   0   0   0  0  0  0  0  0  1  1  1  1
x   x   x   x  x  x  x  x  1  x  x  x  1
x   x   x   x  x  x  x  1  0  x  x  x  1
x   x   x   x  x  x  1  0  0  x  x  x  1
x   x   x   x  x  1  0  0  0  x  x  x  1
x   x   x   x  1  0  0  0  0  x  x  x  1
x   x   x   1  0  0  0  0  0  x  x  x  1
x   x   1   0  0  0  0  0  0  x  x  x  1
x   1   0   0  0  0  0  0  0  x  x  x  1
1   0   0   0  0  0  0  0  0  x  x  x  1
*/

/* Test case Pair 4 ~EN:
A12 A11 A10 A9 A8 A7 A6 A5 A4 A3 A2 A1 ~P4EN
0   0   0   0  0  0  0  0  0  0  0  0  1
0   0   0   0  0  0  0  0  0  0  0  1  1
0   0   0   0  0  0  0  0  0  0  1  0  1
0   0   0   0  0  0  0  0  0  0  1  1  1
0   0   0   0  0  0  0  0  0  1  0  0  1
0   0   0   0  0  0  0  0  0  1  0  1  1
0   0   0   0  0  0  0  0  0  1  1  0  1
0   0   0   0  0  0  0  0  0  1  1  1  0
x   x   x   x  x  x  x  x  1  x  x  x  1
x   x   x   x  x  x  x  1  0  x  x  x  1
x   x   x   x  x  x  1  0  0  x  x  x  1
x   x   x   x  x  1  0  0  0  x  x  x  1
x   x   x   x  1  0  0  0  0  x  x  x  1
x   x   x   1  0  0  0  0  0  x  x  x  1
x   x   1   0  0  0  0  0  0  x  x  x  1
x   1   0   0  0  0  0  0  0  x  x  x  1
1   0   0   0  0  0  0  0  0  x  x  x  1
*/
