// Digital circuit New_Address_Decode.dig as structural Verilog
module New_Address_Decode (
  input  A0,
  input  A1,
  input  A2,
  input  A3,
  input  A4,
  input  A5,
  input  A6,
  input  A7,
  input  A8,
  input  A9,
  input  A10,
  input  A11,
  input  A12,
  input  R_nW,
  input  AS,
  output nRAM2CS,
  output nQ4,
  output nQ5,
  output nQ6,
  output nQ7,
  output nROMCS,
  output RTCCS,
  output RAM1nCS,
  output n1Q0,
  output _02_03_nCS,
  output n1Q2,
  output _06_07_nCS,
  output n1Q4,
  output _0A_0B_nCS,
  output _0C_0D_nCS,
  output _0E_0F_nCS,
  output NC2,
  output NC3,
  output NC1
);

  wire _2_AND_pin1, _2_AND_pin2, _2_AND_pin3, _2_AND_pin9, _2_AND_pin10, _2_AND_pin11, _2_AND_pin12,
       _2_OR_pin3, _2_OR_pin6, _2_OR_pin8, _2_OR_pin9, _2_OR_pin10, _2_OR_pin12, _2_OR_pin13, _3_AND_pin6,
       _3_AND_pin9, _3_AND_pin11, MX1_pin12, MX1_pin13, MX1_pin15, MX2_pin7, MX2_pin9, MX2_pin10, MX2_pin11,
       MX2_pin12, MX2_pin13, MX2_pin14, NOT_pin11, NOT_pin12;

  _74138 MX1 (
    .pin1(A11), .pin2(A12), .pin3(1'b0), .pin4(1'b0), .pin5(1'b0), .pin6(AS), .pin7(nQ7), .pin8(1'b0),
    .pin9(nQ6), .pin10(nQ5), .pin11(nQ4), .pin12(MX1_pin12), .pin13(MX1_pin13), .pin14(nRAM2CS),
    .pin15(MX1_pin15), .pin16(1'b1));
  _7432 _2_OR (
    .pin1(A4), .pin2(A5), .pin3(_2_OR_pin3), .pin4(A6), .pin5(A7), .pin6(_2_OR_pin6), .pin7(1'b0),
    .pin8(_2_OR_pin8), .pin9(_2_OR_pin9), .pin10(_2_OR_pin10), .pin11(NC2), .pin12(_2_OR_pin12),
    .pin13(_2_OR_pin13), .pin14(1'b1));
  // NotConnected on _2_OR_pin13
  // NotConnected on _2_OR_pin12
  _7408 _2_AND (
    .pin1(_2_AND_pin1), .pin2(_2_AND_pin2), .pin3(_2_AND_pin3), .pin4(MX1_pin13), .pin5(MX1_pin12),
    .pin6(nROMCS), .pin7(1'b0), .pin8(NC3), .pin9(_2_AND_pin9), .pin10(_2_AND_pin10), .pin11(_2_AND_pin11),
    .pin12(_2_AND_pin12), .pin13(_2_AND_pin3), .pin14(1'b1));
  // NotConnected on _2_AND_pin10
  // NotConnected on _2_AND_pin9
  _74138 MX2 (
    .pin1(A8), .pin2(A9), .pin3(A10), .pin4(MX1_pin15), .pin5(MX1_pin15), .pin6(AS), .pin7(MX2_pin7),
    .pin8(1'b0), .pin9(MX2_pin9), .pin10(MX2_pin10), .pin11(MX2_pin11), .pin12(MX2_pin12), .pin13(MX2_pin13),
    .pin14(MX2_pin14), .pin15(_2_OR_pin10), .pin16(1'b1));
  _7411 _3_AND (
    .pin1(MX2_pin13), .pin2(MX2_pin12), .pin3(MX2_pin11), .pin4(MX2_pin10), .pin5(MX2_pin9),
    .pin6(_3_AND_pin6), .pin7(1'b0), .pin8(RAM1nCS), .pin9(_3_AND_pin9), .pin10(_3_AND_pin6),
    .pin11(_3_AND_pin11), .pin12(_3_AND_pin11), .pin13(MX2_pin7), .pin14(1'b1));
  _7404 NOT (
    .pin1(_2_AND_pin3), .pin2(_2_OR_pin9), .pin3(_2_OR_pin6), .pin4(_2_AND_pin1), .pin5(MX2_pin14),
    .pin6(_2_AND_pin12), .pin7(1'b0), .pin8(_2_AND_pin2), .pin9(_2_OR_pin3), .pin10(NC1), .pin11(NOT_pin11),
    .pin12(NOT_pin12), .pin13(_2_AND_pin11), .pin14(1'b1));
  // NotConnected on NOT_pin11
  _74138 MX3 (
    .pin1(A1), .pin2(A2), .pin3(A3), .pin4(_2_OR_pin8), .pin5(_2_OR_pin8), .pin6(AS), .pin7(_0E_0F_nCS),
    .pin8(1'b0), .pin9(_0C_0D_nCS), .pin10(_0A_0B_nCS), .pin11(n1Q4), .pin12(_06_07_nCS), .pin13(n1Q2),
    .pin14(_02_03_nCS), .pin15(n1Q0), .pin16(1'b1));
  xor xor_1 (_3_AND_pin9, NOT_pin12, _2_AND_pin12);
  not not_2 (RTCCS, NOT_pin12);

  // Notes on the sheet:
  //   R_nW: Read High, Write Low
  //   AS: Address Select
  //   nRAM2CS: RAM 2 ~CE
  //   nQ4: Unused
  //   nQ5: Unused
  //   nQ6: Unused
  //   nQ7: Unused
  //   n1Q0: Unused
  //   n1Q2: Unused
  //   n1Q4: Unused
  //   NC2: Unused
endmodule

/* Test case ROM ~CS:
AS A12 A11 A10 A9 A8 A7 A6 A5 A4 A3 A2 A1 A0 ~ROMCS
0   X   X   X   X  X  X  X  X  X  X  X  X  X    1
1   1   X   X   X  X  X  X  X  X  X  X  X  X    0
1   0   X   X   X  X  X  X  X  X  X  X  X  X    1
*/

/* Test case RAM 2 ~CS:
AS A12 A11 A10 A9 A8 A7 A6 A5 A4 A3 A2 A1 A0 ~RAM2CS
0   X   X   X   X  X  X  X  X  X  X  X  X  X    1
1   1   X   X   X  X  X  X  X  X  X  X  X  X    1
1   0   1   X   X  X  X  X  X  X  X  X  X  X    0
1   0   0   X   X  X  X  X  X  X  X  X  X  X    1
*/

/* Test case RTC CS:
AS A12 A11 A10 A9 A8 A7 A6 A5 A4 A3 A2 A1 A0 RTCCS
0   X   X   X   X  X  X  X  X  X  X  X  X  X   0
1   0   0   0   0  1  1  X  X  X  X  X  X  X   0
1   0   0   0   0  1  0  1  X  X  X  X  X  X   0
1   0   0   0   0  1  0  0  1  X  X  X  X  X   0
1   0   0   0   0  1  0  0  0  1  X  X  X  X   0
1   0   0   0   0  1  0  0  0  0  X  X  X  X   1
1   X   X   X   X  0  X  X  X  X  X  X  X  X   0
*/

/* Test case RAM 1 ~CS:
AS A12 A11 A10 A9 A8 A7 A6 A5 A4 A3 A2 A1 A0 RAM1~CS
0   X   X   X   X  X  X  X  X  X  X  X  X  X    1
1   1   X   X   X  X  X  X  X  X  X  X  X  X    1
1   0   1   X   X  X  X  X  X  X  X  X  X  X    1
1   0   0   1   X  X  X  X  X  X  X  X  X  X    0
1   0   0   0   1  X  X  X  X  X  X  X  X  X    0
1   0   0   0   0  1  1  X  X  X  X  X  X  X    0
1   0   0   0   0  1  0  1  X  X  X  X  X  X    0
1   0   0   0   0  1  0  0  1  X  X  X  X  X    0
1   0   0   0   0  1  0  0  0  1  X  X  X  X    0
1   0   0   0   0  1  0  0  0  0  X  X  X  X    1
1   0   0   0   0  0  1  X  X  X  X  X  X  X    0
*/

/* Test case ORG RTC CS:
AS A12 A11 A10 A9 A8 A7 A6 A5 A4 RTCCS
1   1   x   x   x  x  x  x  x  x  0
1   0   1   x   x  x  x  x  x  x  0
1   0   0   1   x  x  x  x  x  x  0
1   0   0   0   1  x  x  x  x  1  0
1   0   0   0   0  1  1  x  x  x  0
1   0   0   0   0  1  0  1  x  x  0
1   0   0   0   0  1  0  0  1  x  0
1   0   0   0   0  1  0  0  0  0  1
1   0   0   0   0  0  1  x  x  x  0
1   0   0   0   0  0  0  1  x  x  0
1   0   0   0   0  0  0  0  1  x  0
*/
